// Logisim project item_a.circ as structural Verilog: 1 circuit, main circuit main
module main (
  input  A,
  input  B,
  input  C,
  output X
);

  wire and_1_out, not_1_out;

  not not_1 (not_1_out, A);
  and and_1 (and_1_out, not_1_out, B);
  or or_1 (X, and_1_out, C);

  // Notes on the sheet:
  //   QUESTÃO 1
  //   a)
  //   X = C+~A⋅B
  //   A B C | X        
  //   0 0 0 | 0
  //   0 0 1 | 1
  //   0 1 0 | 1
  //   0 1 1 | 1
  //   1 0 0 | 0
  //   1 0 1 | 1
  //   1 1 0 | 0
  //   1 1 1 | 1
endmodule
