// Logisim project item_b.circ as structural Verilog: 1 circuit, main circuit main
module main (
  input  A,
  input  B,
  input  C,
  output X
);

  wire not_1_out, or_1_out, or_2_out;

  not not_1 (not_1_out, C);
  or or_1 (or_1_out, A, B);
  or or_2 (or_2_out, B, not_1_out);
  and and_1 (X, or_1_out, or_2_out);

  // Notes on the sheet:
  //   QUESTÃO 1
  //   b)
  //   X = B+A⋅~C
  //   A B C | X       
  //   0 0 0 | 0
  //   0 0 1 | 0
  //   0 1 0 | 1
  //   0 1 1 | 1
  //   1 0 0 | 1
  //   1 0 1 | 0
  //   1 1 0 | 1
  //   1 1 1 | 1
endmodule
