// Logisim project item_d.circ as structural Verilog: 1 circuit, main circuit main
module main (
  input  A,
  input  B,
  input  C,
  output X,
  output Y
);

  wire and_1_out, and_2_out, and_3_out;

  ExactlyOne xor_1 (.out(X), .in0(A), .in1(B), .in2(C));
  and and_1 (and_1_out, A, B);
  and and_2 (and_2_out, B, C);
  and and_3 (and_3_out, A, C);
  or or_1 (Y, and_1_out, and_2_out, and_3_out);

  // Notes on the sheet:
  //   QUESTÃO 1
  //   d)
  //   A B C | X Y
  //   0 0 0 | 0 0
  //   0 0 1 | 1 0
  //   0 1 0 | 1 0
  //   0 1 1 | 0 1
  //   1 0 0 | 1 0
  //   1 0 1 | 0 1
  //   1 1 0 | 0 1
  //   1 1 1 | 0 1
  //   X = ~A⋅~B⋅C+~A⋅B⋅~C+A⋅~B⋅~C
  //   Y = B⋅C+A⋅C+A⋅B
endmodule
