// Logisim project item_a.circ as structural Verilog: 1 circuit, main circuit main
module main (
  input  A,
  input  B,
  input  C,
  output X
);

  wire not_1_out, not_2_out, not_3_out, or_1_out;

  not not_1 (not_1_out, A);
  not not_2 (not_2_out, B);
  or or_1 (or_1_out, not_1_out, not_2_out);
  not not_3 (not_3_out, or_1_out);
  and and_1 (X, not_3_out, B, C);

  // Notes on the sheet:
  //   QUESTÃO 2 
  //   PRIMEIRO CIRCUITO (1°)
  //   X = A⋅B⋅C
  //   A   B   C
  //   X
  //   0
  //   0   0   0
  //   0
  //   0   0   1
  //   0   1   0
  //   0
  //   0   1   1
  //   0
  //   1   0   0
  //   0
  //   0
  //   1   0   1
  //   1   1   0
  //   0
  //   1
  //   1   1   1
endmodule
