// Logisim project item_b.circ as structural Verilog: 1 circuit, main circuit main
module main (
  input  A,
  input  B,
  input  C,
  input  D,
  output X
);

  wire and_1_out, and_2_out, and_3_out, not_1_out, not_2_out, not_3_out;

  not not_1 (not_1_out, A);
  not not_2 (not_2_out, B);
  not not_3 (not_3_out, C);
  and and_1 (and_1_out, not_1_out, not_2_out, not_3_out);
  and and_2 (and_2_out, A, not_2_out, not_3_out);
  and and_3 (and_3_out, not_1_out, not_2_out, D);
  or or_1 (X, and_1_out, and_2_out, and_3_out);

  // Notes on the sheet:
  //   QUESTÃO 2
  //   SEGUNDO CIRCUITO (2°)
  //   X = ~B⋅~C+~A⋅~B⋅D
  //   A B C D | X                  
  //   0 0 0 0 | 1
  //   0 0 0 1 | 1
  //   0 0 1 0 | 0
  //   0 0 1 1 | 1
  //   0 1 0 0 | 0
  //    0 1 0 1 | 0
  //   0 1 1 0 | 0
  //   0 1 1 1 | 0
  //   1 0 0 0 | 1
  //   1 0 0 1 | 1
  //   1 0 1 0 | 0
  //   1 0 1 1 | 0
  //   1 1 0 0 | 0
  //   1 1 0 1 | 0
  //   1 1 1 0 | 0
  //   1 1 1 1 | 0
endmodule
