// Logisim project questao04.circ as structural Verilog: 1 circuit, main circuit main
module main (
  input  H,
  input  U,
  input  T,
  input  F,
  output A
);

  wire and_1_out, and_2_out, and_3_out, and_4_out, not_1_out, not_2_out, not_3_out, not_4_out;

  not not_1 (not_1_out, H);
  not not_2 (not_2_out, U);
  not not_3 (not_3_out, T);
  not not_4 (not_4_out, F);
  and and_1 (and_1_out, T, H);
  and and_2 (and_2_out, F, U);
  and and_3 (and_3_out, U, T, F);
  and and_4 (and_4_out, U, T, H);
  or or_1 (A, and_1_out, and_2_out, and_3_out, and_4_out);

  // Notes on the sheet:
  //   QUESTÃO 4
  //   F --> FINAL DE SEMANA
  //   A = U⋅F+H⋅T
  //   LEGENDA
  //   H --> ESTAR ENTRE 9:00h A 17:00h
  //   T --> TEMPERATURA ACIMA DE 21°C
  //   U --> UMIDADE RELATIVA DO AR ACIMA DE 85%
endmodule
